// Logisim project curcuit.circ as structural Verilog: 10 circuits, main circuit main
module main (
);

  wire clck, clock_1_out, dipswitch_1_sw1, HLT, not_1_out, reset;

  and and_1 (clck, clock_1_out, not_1_out);
  not not_1 (not_1_out, dipswitch_1_sw1);
  Clock clock_1 (.out(clock_1_out));
  DipSwitch #(.number(2)) dipswitch_1 (.sw1(dipswitch_1_sw1), .sw2(HLT));
  CPU cpu_1 (.reset(reset), .Clock(clck), .HLT(HLT));
  Button R (.out(reset));
endmodule

module ProgramCounter (
  input  [31:0] JmpAddr,
  input  Reset,
  input  Jmp,
  input  Clock,
  output [31:0] ip
);

  wire [31:0] adder_1_out, multiplexer_1_out;

  Adder #(.width(32)) adder_1 (.a(ip), .b(32'h1), .out(adder_1_out));  // open: cin, cout
  Multiplexer #(.width(32)) multiplexer_1 (.in0(adder_1_out), .in1(JmpAddr), .out(multiplexer_1_out), .sel(Jmp));
  Register #(.width(32)) PC (.D(multiplexer_1_out), .en(1'b1), .Q(ip), .clk(Clock), .clr(Reset));
endmodule

module CPU (
  input  reset,
  input  Clock,
  input  HLT
);

  wire ALU_Calc, button_1_out, clck, DRW, HLT_t, IRI, IRO, JMP, MAI, MI, ML, MO, not_1_out, not_2_out, PCO,
       PCUp, reset_t, SR1O;
  wire [2:0] alu_1_co, flags;
  wire [3:0] ALU_OP, DRID, instrdecoder_1_op, SR1ID, SR2ID;
  wire [23:0] bit_extender_2_out, register_1_q;
  wire [31:0] alu_1_a_o, bit_extender_1_out, bit_extender_3_out, cpu_bus, PC_ip, ram_1_dout, register_2_q,
       SR1, SR2;

  Button button_1 (.out(button_1_out));
  or or_1 (reset_t, button_1_out, reset);
  and and_1 (clck, Clock, ~HLT, ~HLT_t);  // AND_Gate
  assign bit_extender_1_out = {{8{register_1_q[23]}}, register_1_q};  // Bit_Extender bit_extender_1
  not not_1 (not_1_out, not_2_out);
  not not_2 (not_2_out, PCUp);
  Register #(.width(24)) register_1 (.D(bit_extender_2_out), .en(MAI), .clk(clck), .Q(register_1_q), .clr(reset_t));
  Bit_Extender #(.in_width(32), .out_width(24), .\type ("zero")) bit_extender_2 (
    .in(cpu_bus), .out(bit_extender_2_out));
  Register #(.width(32)) register_2 (.D(cpu_bus), .en(IRI), .clk(clck), .Q(register_2_q), .clr(reset_t));
  Multiplexer #(.width(32)) multiplexer_1 (.in1(PC_ip), .out(cpu_bus), .sel(PCO));  // open: in0
  ProgramCounter PC (.JmpAddr(bit_extender_1_out), .Reset(reset_t), .Jmp(JMP), .Clock(not_1_out), .ip(PC_ip));
  RAM #(.addrWidth(24), .dataWidth(32)) ram_1 (
    .addr(register_1_q), .we(MI), .oe(ML), .clk(clck), .din(cpu_bus), .dout(ram_1_dout));
  assign bit_extender_3_out = {{8{1'b0}}, {register_2_q[0], register_2_q[1], register_2_q[2], register_2_q[3], register_2_q[4], register_2_q[5], register_2_q[6], register_2_q[7], register_2_q[8], register_2_q[9], register_2_q[10], register_2_q[11], register_2_q[12], register_2_q[13], register_2_q[14], register_2_q[15], register_2_q[16], register_2_q[17], register_2_q[18], register_2_q[19], register_2_q[20], register_2_q[21], register_2_q[22], register_2_q[23]}};  // Bit_Extender bit_extender_3
  Multiplexer #(.width(32)) multiplexer_2 (.in1(bit_extender_3_out), .out(cpu_bus), .sel(IRO));  // open: in0
  ALU alu_1 (
    .C_or_B(1'b0), .Op(ALU_OP), .N1(SR1), .N2(SR2), .MC({32{1'b0}}), .CO(alu_1_co[0]), .BO(alu_1_co[1]),
    .A_O(alu_1_a_o), .Comp(alu_1_co[2]));  // open: MCO
  Register #(.width(3)) register_3 (.D(alu_1_co), .en(ALU_Calc), .clk(clck), .Q(flags), .clr(reset_t));
  Multiplexer #(.width(32)) multiplexer_3 (.in1(alu_1_a_o), .out(cpu_bus), .sel(ALU_Calc));  // open: in0
  RegisterBank registerbank_1 (
    .C(clck), .R(reset_t), .W(DRW), .RS1(SR1ID), .RS2(SR2ID), .DR(DRID), .DRD(cpu_bus), .S1(SR1), .S2(SR2));
  Multiplexer #(.width(32)) multiplexer_4 (.in1(ram_1_dout), .out(cpu_bus), .sel(MO));  // open: in0
  Multiplexer #(.width(32)) multiplexer_5 (.in1(SR1), .out(cpu_bus), .sel(SR1O));  // open: in0
  InstrDecoder instrdecoder_1 (
    .IR(register_2_q), .flags(flags), .ALUOP(ALU_OP), .DR(DRID), .SR2(SR2ID), .SR1(SR1ID),
    .OP(instrdecoder_1_op));
  Executor executor_1 (
    .OP(instrdecoder_1_op), .clock(clck), .reset(reset_t), .JMP(JMP), .PCU(PCUp), .PCO(PCO), .DRW(DRW),
    .SR1O(SR1O), .ALUCalc(ALU_Calc), .MAI(MAI), .MI(MI), .ML(ML), .MO(MO), .IRI(IRI), .IRO(IRO), .HLT(HLT_t));
endmodule

module ALU (
  input  C_or_B,
  input  [3:0] Op,
  input  [31:0] N1,
  input  [31:0] N2,
  input  [31:0] MC,
  output CO,
  output BO,
  output [31:0] MCO,
  output [31:0] A_O,
  output Comp
);

  wire comparator_1_eq, comparator_1_gt, comparator_1_lt, or_2_out, or_3_out;
  wire [4:0] bit_extender_1_out, bit_extender_2_out, bit_extender_3_out, bit_extender_4_out,
       bit_extender_5_out;
  wire [31:0] adder_1_out, and_1_out, multiplier_1_out, nand_1_out, negator_1_out, not_1_out, or_1_out,
       shifter_1_out, shifter_2_out, shifter_3_out, shifter_4_out, shifter_5_out, subtractor_1_out,
       xnor_1_out, xor_1_out;

  Bit_Extender #(.in_width(32), .out_width(5), .\type ("zero")) bit_extender_1 (.in(N2), .out(bit_extender_1_out));
  Bit_Extender #(.in_width(32), .out_width(5), .\type ("zero")) bit_extender_2 (.in(N2), .out(bit_extender_2_out));
  Bit_Extender #(.in_width(32), .out_width(5), .\type ("zero")) bit_extender_3 (.in(N2), .out(bit_extender_3_out));
  Bit_Extender #(.in_width(32), .out_width(5), .\type ("zero")) bit_extender_4 (.in(N2), .out(bit_extender_4_out));
  Bit_Extender #(.in_width(32), .out_width(5), .\type ("zero")) bit_extender_5 (.in(N2), .out(bit_extender_5_out));
  Adder #(.width(32)) adder_1 (.a(N1), .b(N2), .out(adder_1_out), .cin(C_or_B), .cout(CO));
  Subtractor #(.width(32)) subtractor_1 (.a(N1), .b(N2), .out(subtractor_1_out), .bin(C_or_B), .bout(BO));
  Multiplier #(.width(32)) multiplier_1 (.a(N1), .b(N2), .out(multiplier_1_out), .cin(MC), .cout(MCO));
  Negator #(.width(32)) negator_1 (.in(N1), .out(negator_1_out));
  assign and_1_out = N1 & N2;  // AND_Gate and_1, 32 bits wide
  assign or_1_out = N1 | N2;  // OR_Gate or_1, 32 bits wide
  assign not_1_out = ~N1;  // NOT_Gate not_1, 32 bits wide
  assign nand_1_out = ~(N1 & N2);  // NAND_Gate nand_1, 32 bits wide
  assign xor_1_out = N1 ^ N2;  // XOR_Gate xor_1, 32 bits wide
  assign xnor_1_out = ~(N1 ^ N2);  // XNOR_Gate xnor_1, 32 bits wide
  Shifter #(.width(32)) shifter_1 (.in(N1), .\dist (bit_extender_1_out), .out(shifter_1_out));
  Shifter #(.shift("lr"), .width(32)) shifter_2 (.in(N1), .\dist (bit_extender_2_out), .out(shifter_2_out));
  Shifter #(.shift("ar"), .width(32)) shifter_3 (.in(N1), .\dist (bit_extender_3_out), .out(shifter_3_out));
  Shifter #(.shift("rl"), .width(32)) shifter_4 (.in(N1), .\dist (bit_extender_4_out), .out(shifter_4_out));
  Shifter #(.shift("rr"), .width(32)) shifter_5 (.in(N1), .\dist (bit_extender_5_out), .out(shifter_5_out));
  Comparator #(.mode("unsigned"), .width(32)) comparator_1 (
    .a(N1), .b(N2), .gt(comparator_1_gt), .eq(comparator_1_eq), .lt(comparator_1_lt));
  or or_2 (or_2_out, comparator_1_gt, comparator_1_eq);
  or or_3 (or_3_out, comparator_1_eq, comparator_1_lt);
  Multiplexer #(.select(4), .width(32)) multiplexer_1 (
    .in0(adder_1_out), .in1(subtractor_1_out), .in2(multiplier_1_out), .in3(negator_1_out), .in4(and_1_out),
    .in5(or_1_out), .in6(not_1_out), .in7(nand_1_out), .in8(xor_1_out), .in9(xnor_1_out),
    .in10(shifter_1_out), .in11(shifter_2_out), .in12(shifter_3_out), .in13(shifter_4_out),
    .in14(shifter_5_out), .in15({32{1'b0}}), .out(A_O), .sel(Op));
  Multiplexer #(.select(4)) multiplexer_2 (
    .in0(comparator_1_gt), .in1(comparator_1_eq), .in2(comparator_1_lt), .in3(or_2_out), .in4(or_3_out),
    .in5(1'b0), .in6(1'b0), .in7(1'b0), .in8(1'b0), .in9(1'b0), .in10(1'b0), .in11(1'b0), .in12(1'b0),
    .in13(1'b0), .in14(1'b0), .in15(1'b0), .out(Comp), .sel(Op));
endmodule

module RegisterBank (
  input  C,
  input  R,
  input  W,
  input  [3:0] RS1,
  input  [3:0] RS2,
  input  [3:0] DR,
  input  [31:0] DRD,
  output [31:0] S1,
  output [31:0] S2
);

  wire and_1_out, and_2_out, and_3_out, and_4_out, and_5_out, and_6_out, and_7_out, and_8_out, and_9_out,
       and_10_out, and_11_out, and_12_out, and_13_out, and_14_out, and_15_out, and_16_out, decoder_1_out0,
       decoder_1_out1, decoder_1_out2, decoder_1_out3, decoder_1_out4, decoder_1_out5, decoder_1_out6,
       decoder_1_out7, decoder_1_out8, decoder_1_out9, decoder_1_out10, decoder_1_out11, decoder_1_out12,
       decoder_1_out13, decoder_1_out14, decoder_1_out15;
  wire [31:0] register_1_q, register_2_q, register_3_q, register_4_q, register_5_q, register_6_q,
       register_7_q, register_8_q, register_9_q, register_10_q, register_11_q, register_12_q, register_13_q,
       register_14_q, register_15_q, register_16_q;

  Decoder #(.enable("false"), .select(4)) decoder_1 (
    .out0(decoder_1_out0), .out1(decoder_1_out1), .out2(decoder_1_out2), .out3(decoder_1_out3),
    .out4(decoder_1_out4), .out5(decoder_1_out5), .out6(decoder_1_out6), .out7(decoder_1_out7),
    .out8(decoder_1_out8), .out9(decoder_1_out9), .out10(decoder_1_out10), .out11(decoder_1_out11),
    .out12(decoder_1_out12), .out13(decoder_1_out13), .out14(decoder_1_out14), .out15(decoder_1_out15),
    .sel(DR));
  Register #(.width(32)) register_1 (.D(DRD), .en(and_1_out), .clk(C), .Q(register_1_q), .clr(R));
  and and_1 (and_1_out, decoder_1_out0, W);
  Register #(.width(32)) register_2 (.D(DRD), .en(and_2_out), .clk(C), .Q(register_2_q), .clr(R));
  and and_2 (and_2_out, decoder_1_out1, W);
  Register #(.width(32)) register_3 (.D(DRD), .en(and_3_out), .clk(C), .Q(register_3_q), .clr(R));
  and and_3 (and_3_out, decoder_1_out2, W);
  and and_4 (and_4_out, decoder_1_out3, W);
  and and_5 (and_5_out, decoder_1_out4, W);
  and and_6 (and_6_out, decoder_1_out5, W);
  Register #(.width(32)) register_4 (.D(DRD), .en(and_4_out), .clk(C), .Q(register_4_q), .clr(R));
  Register #(.width(32)) register_5 (.D(DRD), .en(and_5_out), .clk(C), .Q(register_5_q), .clr(R));
  Register #(.width(32)) register_6 (.D(DRD), .en(and_6_out), .clk(C), .Q(register_6_q), .clr(R));
  Register #(.width(32)) register_7 (.D(DRD), .en(and_7_out), .clk(C), .Q(register_7_q), .clr(R));
  and and_7 (and_7_out, decoder_1_out6, W);
  Register #(.width(32)) register_8 (.D(DRD), .en(and_8_out), .clk(C), .Q(register_8_q), .clr(R));
  and and_8 (and_8_out, decoder_1_out7, W);
  Register #(.width(32)) register_9 (.D(DRD), .en(and_9_out), .clk(C), .Q(register_9_q), .clr(R));
  and and_9 (and_9_out, decoder_1_out8, W);
  Register #(.width(32)) register_10 (.D(DRD), .en(and_10_out), .clk(C), .Q(register_10_q), .clr(R));
  and and_10 (and_10_out, decoder_1_out9, W);
  Register #(.width(32)) register_11 (.D(DRD), .en(and_11_out), .clk(C), .Q(register_11_q), .clr(R));
  and and_11 (and_11_out, decoder_1_out10, W);
  and and_12 (and_12_out, decoder_1_out11, W);
  and and_13 (and_13_out, decoder_1_out12, W);
  and and_14 (and_14_out, decoder_1_out13, W);
  Register #(.width(32)) register_12 (.D(DRD), .en(and_12_out), .clk(C), .Q(register_12_q), .clr(R));
  Register #(.width(32)) register_13 (.D(DRD), .en(and_13_out), .clk(C), .Q(register_13_q), .clr(R));
  Register #(.width(32)) register_14 (.D(DRD), .en(and_14_out), .clk(C), .Q(register_14_q), .clr(R));
  Register #(.width(32)) register_15 (.D(DRD), .en(and_15_out), .clk(C), .Q(register_15_q), .clr(R));
  and and_15 (and_15_out, decoder_1_out14, W);
  Register #(.width(32)) register_16 (.D(DRD), .en(and_16_out), .clk(C), .Q(register_16_q), .clr(R));
  and and_16 (and_16_out, decoder_1_out15, W);
  Multiplexer #(.select(4), .width(32)) multiplexer_1 (
    .in0(register_1_q), .in1(register_2_q), .in2(register_3_q), .in3(register_4_q), .in4(register_5_q),
    .in5(register_6_q), .in6(register_7_q), .in7(register_8_q), .in8(register_9_q), .in9(register_10_q),
    .in10(register_11_q), .in11(register_12_q), .in12(register_13_q), .in13(register_14_q),
    .in14(register_15_q), .in15(register_16_q), .out(S1), .sel(RS1));
  Multiplexer #(.select(4), .width(32)) multiplexer_2 (
    .in0(register_1_q), .in1(register_2_q), .in2(register_3_q), .in3(register_4_q), .in4(register_5_q),
    .in5(register_6_q), .in6(register_7_q), .in7(register_8_q), .in8(register_9_q), .in9(register_10_q),
    .in10(register_11_q), .in11(register_12_q), .in12(register_13_q), .in13(register_14_q),
    .in14(register_15_q), .in15(register_16_q), .out(S2), .sel(RS2));

  // Notes on the sheet:
  //   R0
  //   R1
  //   R2
  //   R3
  //   R4
  //   R5
  //   R6
  //   R7
  //   R8\
  //   R9
  //   R10
  //   R11
  //   R12
  //   R13
  //   R14
  //   Tmp/Dump
endmodule

module InstrDecoder (
  input  [31:0] IR,
  input  [2:0] flags,
  output [3:0] ALUOP,
  output [3:0] DR,
  output [3:0] SR2,
  output [3:0] SR1,
  output [3:0] OP
);

  wire instrdecoderca_1_sr1tdr;

  InstrDecoderCA instrdecoderca_1 (
    .OP(IR[31:28]), .JMPIF(IR[21:20]), .carry(flags[0]), .comp(flags[2]), .POP(OP),
    .SR1TDR(instrdecoderca_1_sr1tdr));
  Multiplexer #(.width(4)) multiplexer_1 (.in0(IR[19:16]), .in1(IR[27:24]), .out(DR), .sel(instrdecoderca_1_sr1tdr));

  assign ALUOP = IR[15:12];
  assign SR1 = IR[27:24];
  assign SR2 = IR[23:20];

  // Other names for the same wires on the sheet: carry = flags[0]; comp = flags[2]
endmodule

module counter_3_bit (
  input  C,
  input  R,
  output [2:0] count
);

  wire j_k_ff_1_qn, j_k_ff_2_qn, j_k_ff_3_qn, not_1_out, not_2_out, not_3_out;

  J_K_Flip_Flop j_k_ff_1 (
    .J(j_k_ff_1_qn), .K(not_1_out), .clk(C), .Q(count[0]), .Qn(j_k_ff_1_qn), .reset(R));  // open: preset
  not not_1 (not_1_out, j_k_ff_1_qn);
  J_K_Flip_Flop j_k_ff_2 (
    .J(j_k_ff_2_qn), .K(not_2_out), .clk(j_k_ff_1_qn), .Q(count[1]), .Qn(j_k_ff_2_qn), .reset(R));  // open: preset
  not not_2 (not_2_out, j_k_ff_2_qn);
  J_K_Flip_Flop j_k_ff_3 (
    .J(j_k_ff_3_qn), .K(not_3_out), .clk(j_k_ff_2_qn), .Q(count[2]), .Qn(j_k_ff_3_qn), .reset(R));  // open: preset
  not not_3 (not_3_out, j_k_ff_3_qn);
endmodule

module InstrDecoderCA (
  input  [3:0] OP,
  input  [1:0] JMPIF,
  input  carry,
  input  comp,
  output [3:0] POP,
  output SR1TDR
);

  wire and_1_out, and_2_out, and_3_out, and_4_out, and_5_out, and_6_out, and_7_out, and_8_out, and_9_out,
       and_10_out, and_11_out, and_12_out, not_1_out, not_2_out, not_3_out, not_4_out, not_5_out, not_6_out;

  not not_1 (not_1_out, OP[3]);
  not not_2 (not_2_out, OP[1]);
  not not_3 (not_3_out, OP[0]);
  not not_4 (not_4_out, JMPIF[1]);
  not not_5 (not_5_out, JMPIF[0]);
  not not_6 (not_6_out, comp);
  and and_1 (and_1_out, OP[1], not_3_out);
  and and_2 (and_2_out, OP[1], not_4_out, not_5_out);
  and and_3 (and_3_out, OP[1], not_4_out, carry);
  and and_4 (and_4_out, OP[1], not_5_out, comp);
  and and_5 (and_5_out, OP[1], JMPIF[1], JMPIF[0], not_6_out);
  and and_6 (and_6_out, OP[2], OP[1]);
  and and_7 (and_7_out, OP[3], OP[1]);
  and and_8 (and_8_out, not_2_out, OP[0]);
  and and_9 (and_9_out, OP[0], not_4_out, not_5_out);
  and and_10 (and_10_out, OP[0], not_4_out, carry);
  and and_11 (and_11_out, OP[2], OP[0]);
  and and_12 (and_12_out, OP[3], OP[0]);
  and and_13 (SR1TDR, not_1_out, OP[2], not_3_out);
  or or_1 (POP[1], and_1_out, and_2_out, and_3_out, and_4_out, and_5_out, and_6_out, and_7_out);
  or or_2 (POP[0], and_8_out, and_9_out, and_10_out, and_11_out, and_12_out);

  assign POP[3:2] = OP[3:2];
endmodule

module Executor (
  input  [3:0] OP,
  input  clock,
  input  reset,
  output JMP,
  output PCU,
  output PCO,
  output DRW,
  output SR1O,
  output ALUCalc,
  output MAI,
  output MI,
  output ML,
  output MO,
  output IRI,
  output IRO,
  output HLT
);

  wire executorca_1_rsc, or_1_out;
  wire [2:0] counter_3_bit_1_count;

  or or_1 (or_1_out, reset, executorca_1_rsc);
  counter_3_bit counter_3_bit_1 (.C(clock), .R(or_1_out), .count(counter_3_bit_1_count));
  ExecutorCA executorca_1 (
    .OP(OP), .SBC(counter_3_bit_1_count), .JMP(JMP), .PCU(PCU), .PCO(PCO), .DRW(DRW), .SR1O(SR1O),
    .ALUCalc(ALUCalc), .MAI(MAI), .MI(MI), .ML(ML), .MO(MO), .IRI(IRI), .IRO(IRO), .HLT(HLT),
    .RSC(executorca_1_rsc));
endmodule

module ExecutorCA (
  input  [3:0] OP,
  input  [2:0] SBC,
  output JMP,
  output PCU,
  output PCO,
  output DRW,
  output SR1O,
  output ALUCalc,
  output MAI,
  output MI,
  output ML,
  output MO,
  output IRI,
  output IRO,
  output HLT,
  output RSC
);

  wire and_2_out, and_3_out, and_5_out, and_6_out, and_7_out, and_8_out, and_9_out, and_10_out, and_11_out,
       and_12_out, and_13_out, and_14_out, and_15_out, and_16_out, and_17_out, and_18_out, and_19_out,
       and_20_out, and_21_out, and_22_out, and_23_out, and_24_out, and_26_out, and_27_out, and_28_out,
       and_29_out, and_30_out, and_31_out, and_32_out, and_33_out, and_34_out, and_35_out, and_36_out,
       and_37_out, not_1_out, not_2_out, not_3_out, not_4_out, not_5_out, not_6_out, not_7_out;

  not not_1 (not_1_out, OP[3]);
  not not_2 (not_2_out, OP[2]);
  not not_3 (not_3_out, OP[1]);
  not not_4 (not_4_out, OP[0]);
  not not_5 (not_5_out, SBC[2]);
  not not_6 (not_6_out, SBC[1]);
  not not_7 (not_7_out, SBC[0]);
  and and_1 (JMP, not_1_out, not_2_out, OP[1], OP[0], SBC[2], not_6_out, not_7_out);
  and and_2 (and_2_out, not_5_out, not_6_out, SBC[0]);
  and and_3 (and_3_out, not_1_out, not_2_out, OP[1], OP[0], SBC[2], not_6_out, not_7_out);
  and and_4 (PCO, not_5_out, not_6_out, not_7_out);
  and and_5 (and_5_out, not_1_out, OP[2], OP[1], not_4_out, not_5_out, SBC[1], SBC[0]);
  and and_6 (and_6_out, not_1_out, OP[2], not_3_out, SBC[2], not_6_out, SBC[0]);
  and and_7 (and_7_out, not_2_out, not_3_out, OP[0], not_5_out, SBC[1], SBC[0]);
  and and_8 (and_8_out, OP[3], not_2_out, not_3_out, not_5_out, SBC[1], SBC[0]);
  and and_9 (and_9_out, OP[3], not_2_out, not_3_out, not_4_out, SBC[2], not_6_out, not_7_out);
  and and_10 (and_10_out, not_1_out, not_2_out, OP[1], OP[0], not_5_out, SBC[1], SBC[0]);
  and and_11 (and_11_out, not_1_out, OP[2], not_3_out, OP[0], not_5_out, SBC[1], SBC[0]);
  and and_12 (and_12_out, not_1_out, OP[2], OP[1], OP[0], SBC[2], not_6_out, not_7_out);
  and and_13 (and_13_out, not_1_out, not_2_out, OP[1], not_4_out, not_5_out, SBC[1], SBC[0]);
  and and_14 (and_14_out, not_1_out, not_2_out, not_3_out, OP[0], not_5_out, SBC[1], SBC[0]);
  and and_15 (and_15_out, not_5_out, not_6_out, not_7_out);
  and and_16 (and_16_out, not_1_out, OP[2], not_3_out, not_5_out, SBC[1], SBC[0]);
  and and_17 (and_17_out, OP[3], not_2_out, not_3_out, not_4_out, not_5_out, SBC[1], SBC[0]);
  and and_18 (and_18_out, not_1_out, OP[1], OP[0], not_5_out, SBC[1], SBC[0]);
  and and_19 (and_19_out, OP[3], not_2_out, not_3_out, not_4_out, SBC[2], not_6_out, not_7_out);
  and and_20 (and_20_out, not_1_out, OP[2], OP[1], OP[0], SBC[2], not_6_out, not_7_out);
  and and_21 (and_21_out, not_5_out, not_6_out, SBC[0]);
  and and_22 (and_22_out, not_1_out, OP[2], not_3_out, SBC[2], not_6_out, not_7_out);
  and and_23 (and_23_out, not_5_out, SBC[1], not_7_out);
  and and_24 (and_24_out, not_1_out, OP[2], not_3_out, SBC[2], not_6_out, SBC[0]);
  and and_25 (IRI, not_5_out, SBC[1], not_7_out);
  and and_26 (and_26_out, not_1_out, OP[2], not_4_out, not_5_out, SBC[1], SBC[0]);
  and and_27 (and_27_out, not_1_out, OP[2], OP[1], not_5_out, SBC[1], SBC[0]);
  and and_28 (and_28_out, OP[3], OP[1], SBC[1], SBC[0]);
  and and_29 (and_29_out, OP[3], OP[1], SBC[2]);
  and and_30 (and_30_out, OP[3], OP[2], SBC[1], SBC[0]);
  and and_31 (and_31_out, OP[3], OP[2], SBC[2]);
  and and_32 (and_32_out, not_1_out, OP[1], not_4_out, SBC[2], not_6_out, not_7_out);
  and and_33 (and_33_out, OP[3], not_2_out, not_3_out, not_4_out, SBC[2], not_6_out, SBC[0]);
  and and_34 (and_34_out, not_1_out, OP[2], not_3_out, SBC[2], SBC[1], not_7_out);
  and and_35 (and_35_out, not_1_out, not_2_out, not_3_out, not_4_out, SBC[2], SBC[1], SBC[0]);
  and and_36 (and_36_out, not_2_out, not_3_out, OP[0], SBC[2], not_6_out, not_7_out);
  and and_37 (and_37_out, not_1_out, OP[1], OP[0], SBC[2], not_6_out, SBC[0]);
  or or_1 (PCU, and_2_out, and_3_out);
  or or_2 (DRW, and_5_out, and_6_out, and_7_out);
  or or_3 (SR1O, and_8_out, and_9_out, and_10_out, and_11_out, and_12_out);
  or or_4 (ALUCalc, and_13_out, and_14_out);
  or or_5 (MAI, and_15_out, and_16_out, and_17_out, and_18_out);
  or or_6 (MI, and_19_out, and_20_out);
  or or_7 (ML, and_21_out, and_22_out);
  or or_8 (MO, and_23_out, and_24_out);
  or or_9 (IRO, and_26_out, and_27_out);
  or or_10 (HLT, and_28_out, and_29_out, and_30_out, and_31_out);
  or or_11 (RSC, and_32_out, and_33_out, and_34_out, and_35_out, and_36_out, and_37_out);
endmodule
